# Fritzing sketch RTC_SD_RS232_shield (saved by Fritzing 0.9.2b)
circuit board: 8.46667cm x 5.64444cm

parts:
  Composant1 = Memoire 1.0 - SD card log shield
  U1 = MAX3323 [package="DIP16 [THT]"]
  C1 = Electrolytic Capacitor [capacitance=1µF package="100 mil [THT, electrolytic]"]
  C2 = Electrolytic Capacitor [capacitance=1µF package="100 mil [THT, electrolytic]"]
  C3 = Electrolytic Capacitor [capacitance=1µF package="100 mil [THT, electrolytic]"]
  C4 = Electrolytic Capacitor [capacitance=1µF package="100 mil [THT, electrolytic]"]
  X2 = DB9 Connector [package=db9]

nets:
  N1: Composant1.DIG_6, Composant1.N$102, U1.ROUT1
  N2: Composant1.DIG_7, Composant1.N$57, U1.TIN1
  +5V: Composant1.+5V, Composant1.N$18, Composant1.N$19, Composant1.N$20, Composant1.N$36, Composant1.N$37, Composant1.N$50, Composant1.N$58, Composant1.N$59, Composant1.N$60, Composant1.N$61, Composant1.N$62, U1.TXENABLE, U1.RENABLE, U1.VL, U1.SHDN', U1.VCC
  N3: Composant1.GND, C3.-, C4.-, X2.5_-_GND
  N4: Composant1.N$24, Composant1.N$42, Composant1.N$85, U1.V+, C4.+
  N5: Composant1.N$44, U1.RIN1, X2.2_-_RXD
  N6: Composant1.N$56, Composant1.N$81, Composant1.N$97, U1.V-, C3.+
  N7: Composant1.N$63, U1.GND
  N8: Composant1.N$83, U1.C2+, C2.+
  N9: Composant1.N$90, U1.TOUT1, X2.3_-_TXD
  N10: Composant1.N$91, U1.C2-, C2.-
  N11: Composant1.N$92, U1.C1-, C1.-
  N12: Composant1.N$93, U1.C1+, C1.+
  N13: X2.1_-_DCD, X2.4_-_DTR, X2.6_-_DSR
  N14: X2.7_-_RTS, X2.8_-_CTS

custom parts:
  MAX3323: RS-232 driver/receiver
  DB9 Connector: DB9 Connector Standard DB9 (D-Sub 9) serial connector. Can be used for CAN bus as well as RS485 and RS232. Footprint production proven. Spark Fun Electronics SKU : PRT-00429
